// Logisim project Silverback.circ as structural Verilog: 1 circuit, main circuit main
module main (
);

  wire and_2_out, and_3_out, and_4_out, comparator_1_eq, comparator_2_eq, comparator_3_eq, decoder_1_out0,
       decoder_1_out1, decoder_1_out2, decoder_1_out3, not_1_out, TheClock_out;
  wire [7:0] adder_1_out, adder_2_out, bit_extender_1_out, DataMem_dout, multiplexer_1_out,
       multiplexer_2_out, multiplexer_3_out, multiplexer_4_out, multiplexer_5_out, PC_q, R0_q, R1_q, R2_q,
       R3_q, rom_1_data, subtractor_1_out;

  Clock TheClock (.out(TheClock_out));
  Adder adder_1 (.a(PC_q), .b(8'h1), .out(adder_1_out));  // open: cin, cout
  Register PC (.D(adder_1_out), .clk(TheClock_out), .Q(PC_q));  // open: en, clr
  RAM DataMem (
    .addr(multiplexer_5_out), .we(comparator_1_eq), .oe(comparator_2_eq), .clk(TheClock_out),
    .din(multiplexer_3_out), .dout(DataMem_dout));
  ROM rom_1 (.addr(PC_q), .data(rom_1_data));
  Decoder #(.select(2)) decoder_1 (
    .out0(decoder_1_out0), .out1(decoder_1_out1), .out2(decoder_1_out2), .out3(decoder_1_out3),
    .sel(rom_1_data[5:4]));  // open: en
  and and_1 (decoder_1_out0, decoder_1_out0, not_1_out);
  and and_2 (and_2_out, decoder_1_out1, not_1_out);
  buf and_3 (and_3_out, decoder_1_out2);  // AND_Gate
  and and_4 (and_4_out, decoder_1_out3, not_1_out);
  Comparator #(.width(2)) comparator_1 (.a(rom_1_data[7:6]), .b(2'b11), .eq(comparator_1_eq));  // open: gt, lt
  not not_1 (not_1_out, comparator_1_eq);
  Register R0 (.D(multiplexer_1_out), .en(decoder_1_out0), .clk(TheClock_out), .Q(R0_q));  // open: clr
  Register R1 (.D(multiplexer_1_out), .en(and_2_out), .clk(TheClock_out), .Q(R1_q));  // open: clr
  Register R2 (.D(multiplexer_1_out), .en(and_3_out), .clk(TheClock_out), .Q(R2_q));  // open: clr
  Register R3 (.D(multiplexer_1_out), .en(and_4_out), .clk(TheClock_out), .Q(R3_q));  // open: clr
  Multiplexer #(.width(8)) multiplexer_1 (
    .in0(multiplexer_5_out), .in1(DataMem_dout), .out(multiplexer_1_out), .sel(comparator_2_eq));
  Comparator #(.width(2)) comparator_2 (.a(rom_1_data[7:6]), .b(2'b10), .eq(comparator_2_eq));  // open: gt, lt
  Comparator #(.width(2)) comparator_3 (.a(rom_1_data[7:6]), .b(2'b01), .eq(comparator_3_eq));  // open: gt, lt
  Multiplexer #(.select(2), .width(8)) multiplexer_2 (
    .in0(R0_q), .in1(R1_q), .in2(R2_q), .in3(R3_q), .out(multiplexer_2_out), .sel(rom_1_data[3:2]));
  Multiplexer #(.select(2), .width(8)) multiplexer_3 (
    .in0(R0_q), .in1(R1_q), .in2(R2_q), .in3(R3_q), .out(multiplexer_3_out), .sel(rom_1_data[1:0]));
  assign bit_extender_1_out = {{6{1'b0}}, rom_1_data[1:0]};  // Bit_Extender bit_extender_1
  Multiplexer #(.width(8)) multiplexer_4 (
    .in0(multiplexer_3_out), .in1(bit_extender_1_out), .out(multiplexer_4_out));  // open: sel
  Adder adder_2 (.a(multiplexer_2_out), .b(multiplexer_4_out), .out(adder_2_out));  // open: cin, cout
  Subtractor subtractor_1 (.a(multiplexer_4_out), .b(multiplexer_2_out), .out(subtractor_1_out));  // open: bin, bout
  Multiplexer #(.width(8)) multiplexer_5 (
    .in0(adder_2_out), .in1(subtractor_1_out), .out(multiplexer_5_out), .sel(comparator_3_eq));

  // Notes on the sheet:
  //   Emiliano Gutierrez
  //   I pledge my honor that I have abided by the Stevens Honor System. 
  //   contents of rom_1 (hex, n*v repeats v):
  //   80 91 21 e2 78 f3
  //   RegDecoder
  //   WB MUX
  //   ALU input A
  //   ALU input B
  //   MUX ALU
endmodule
